# Fritzing sketch Kondensator_und_LCD (saved by Fritzing 0.9.10b)
breadboards: 1

parts:
  U1 = LCD-16X2 [package=lcd-16x2_noholes]
  Part1 = Arduino Uno (Rev3) - ICSP
  C1 = Electrolytic Capacitor [capacitance=10μF voltage=35V package="0605 [SMD, electrolytic]"]
  R1 = Rotary Potentiometer (Small) [maximum_resistance=100kΩ knob_status=50% power=0.5W package=THT]
  R2 = Resistor [tolerance=±5% power=0.25 resistance=220 package=THT]
  R3 = Resistor [tolerance=±5% resistance=220 package="2010 [SMD]"]

nets:
  VSS: U1.VSS, U1.R_W, U1.K, Part1.GND, C1.+, R1.leg2
  VDD: U1.VDD, Part1.5V, R1.leg1, R3.Pin_1
  N1: U1.VO, R1.wiper
  N2: U1.RS, Part1.D11_PWM/MOSI
  N3: U1.E, Part1.D12/MISO
  N4: U1.DB4, Part1.D2
  N5: U1.DB5, Part1.D3_PWM
  N6: U1.DB6, Part1.D4
  N7: U1.DB7, Part1.D5_PWM
  N8: U1.A, R3.Pin_0
  N9: Part1.A0, C1.-, R2.Pin_1
  N10: Part1.D13/SCK, R2.Pin_0

// code stored in the sketch: Kondensator.ino
#define PrueferPin A0
#define Aufladen   13
//#define Entladung  11   //beschleunigt den entladevorgang
/*
#define rs= 11
#define en= 12
#define d4= 2
#define d5= 3
#define d6= 4
#define d7= 5
*/

 #include <LiquidCrystal.h>

 // Die Bibliothek initialisieren und festlegen, welcher
 // Pin des Displays mit welchem Pin auf dem Board verbunden ist:
 const int rs = 11, en = 12, d4 = 2, d5 = 3, d6 = 4, d7 = 5;
 LiquidCrystal lcd(rs, en, d4, d5, d6, d7);

const double Widerstandswert = 10000.0;// Widerstandswert am auflade Pin (hier 10k OHM)
int durchgangsCount = 1;
unsigned long laufStart, entladeStart, deltaZeit, deltaentladeZeit, sumAuf = 0, sumEnt = 0;
double Farads, sumFarads = 0.0;

void setup()
{
   // Festlegen, wie viele Zeichen und Reihen das Display hat:
   lcd.begin(16, 2);
   // "hello, world!" an das Display senden:
// lcd.print("hello, world!");
   
    pinMode(Aufladen, OUTPUT);
    digitalWrite(Aufladen, LOW);
    Serial.begin(9600);
}

void loop()
{
     // Den Cursor in (Spalte 0, Reihe 0) setzen:
   // (Wichtig: Reihe 0 ist die 1. Reihe, da ab 0 gezählt wird):
   
   
   delay(1000);
   lcd.clear();

//MittelwertFunktion
if (durchgangsCount > 16){
  //for(int i = 0; i < durchgangsCount; i++){
   lcd.clear();
   lcd.setCursor(0, 0);
   lcd.print("deltaAufladezeit");
   lcd.setCursor(0, 1);
   lcd.print(sumAuf/durchgangsCount);
   lcd.print(" ms");

    delay(5000);

   lcd.clear();
   lcd.setCursor(0, 0);
   lcd.print("deltaKapazitaet");
   lcd.setCursor(0, 1);
   lcd.print(sumFarads/durchgangsCount);
   lcd.print(" mikroF");

    delay(5000);

   lcd.clear();
   lcd.setCursor(0, 0);
   lcd.print("deltaEntladezeit");
   lcd.setCursor(0, 1);
   lcd.print(sumEnt/durchgangsCount);
   lcd.print(" ms");

    delay(5000);

    
    //}
  
  }
 else{  
   if(durchgangsCount > 1){
   lcd.setCursor(0, 0);
   lcd.print(durchgangsCount);
   lcd.print(". entladezeit:");
   lcd.setCursor(0, 1);
   lcd.print(deltaentladeZeit);
   lcd.print(" ms");
   }

   
   

    Serial.print(durchgangsCount);
    Serial.println(". Durchlauf");
    digitalWrite(Aufladen, HIGH); // beginnt den Aufladeprozess
    laufStart = millis();           // setzt die Zeit 

    while(analogRead(PrueferPin) < 648) {
        // Wartet bis der Kondensator 63.2% geladen ist
    }

    deltaZeit = millis() - laufStart; // vergangene Zeit = gesamtVergangezeit - die bei Anfangs des Durchgang gesetzt 
    Farads = (deltaZeit / Widerstandswert) * 1000; // *1000, weil milli(sekunde) * 1000 = mirko 

    sumFarads = sumFarads + Farads;
    sumAuf = sumAuf + deltaZeit;

    lcd.clear();
    lcd.setCursor(0, 0);
    lcd.print(durchgangsCount);
    lcd.print(". aufladezeit:");
    lcd.setCursor(0, 1);
    lcd.print(deltaZeit);
    lcd.print(" ms");
    
    Serial.print("Aufladedauer:   ");
    Serial.print(deltaZeit);
    Serial.println(" ms    ");

    Serial.print("Kapazität:      "); 
    Serial.print(Farads); 
    Serial.println(" µF");

    digitalWrite(Aufladen, LOW); // beendet den Aufladeprozes
    //pinMode(Entladung, OUTPUT);
    //digitalWrite(Entladung, LOW); // beschleunigt den Entladevorgang (geringer Widerstand)
    entladeStart = millis();
    
    while(analogRead(PrueferPin) > 0) {
        // lässt das Programm nicht weiter bis der Kondensator entladen ist
    }


    lcd.clear();
    lcd.setCursor(0, 0);
    lcd.print(durchgangsCount);
    lcd.print(". kapazitaet:");
    lcd.setCursor(0, 1);
    lcd.print(Farads);
    lcd.print(" mikroF");

  
    
    deltaentladeZeit = millis() - entladeStart;
    sumEnt = sumEnt + deltaentladeZeit;

  

    
    Serial.print("Entladedauer:   ");
    Serial.print(deltaentladeZeit);
    Serial.println("   ms");
    Serial.println();
    
  //  pinMode(Entladung, INPUT); 
  //  digitalWrite(Entladung, HIGH); 
    durchgangsCount++;

}
}

    // Serial.println(C = Q / U); U = 5V,
